# Fritzing sketch ArduinoNano-bmi160-i2c (saved by Fritzing 0.9.6b)
breadboards: 1

parts:
  A1 = BMI160 breakout
  Part2 = Arduino Nano (Rev3.0)

nets:
  N1: A1.Pin_6, A1.Pin_11, Part2.3V3
  N2: A1.Pin_8, A1.Pin_12, Part2.GND
  N3: A1.Pin_9, Part2.A4
  N4: A1.Pin_10, Part2.A5

custom parts:
  BMI160 breakout: BMI160 Latest Stance Accelerometer Gyroscope module 6 Dof inertial Measurement Sensors.
