# Fritzing sketch ArduinoUno-bmi160-i2c (saved by Fritzing 0.9.6b)
breadboards: 1

parts:
  Part1 = Arduino Uno (Rev3)
  A1 = BMI160 breakout

nets:
  N1: Part1.A4/SDA, A1.Pin_10
  N2: Part1.A5/SCL, A1.Pin_9
  N3: Part1.3V3, A1.Pin_6, A1.Pin_11
  N4: Part1.GND, A1.Pin_8, A1.Pin_12

custom parts:
  BMI160 breakout: BMI160 Latest Stance Accelerometer Gyroscope module 6 Dof inertial Measurement Sensors.
